# Fritzing sketch d1mini (saved by Fritzing 0.9.3b)
circuit board: 8.46667cm x 5.64444cm
breadboards: 1

parts:
  WeMos_D1_Mini1 = WeMos D1 Mini
  DHT1 = DHT22 Humidity and Temperature Sensor

nets:
  3V3: WeMos_D1_Mini1.3V3, DHT1.VDD
  N1: WeMos_D1_Mini1.D0, WeMos_D1_Mini1.RST
  N2: WeMos_D1_Mini1.D2, DHT1.DATA
  N3: WeMos_D1_Mini1.G, DHT1.GND
