# Fritzing sketch hardware (saved by Fritzing 0.9.3b)
circuit board: 8.46667cm x 5.64444cm
breadboards: 1

parts:
  U1 = NodeMCU V1.0
  DHT1 = DHT22 Humidity and Temperature Sensor

nets:
  N1: U1.D0, U1.RST
  N2: U1.D2, DHT1.DATA
  3V3: U1.3V3, DHT1.VDD
  N3: U1.GND, DHT1.NULL

custom parts:
  NodeMCU V1.0: ESP8266 based NodeMCU
